// Digital circuit MIPS32SOC.dig as structural Verilog
module MIPS32SOC (
  input  rst,
  input  clk,
  output invalid_opcode,
  output invalid_pc,
  output invalid_addr
);

  wire aluSrc, and_1_out, and_2_out, Bne, Branch_Out, bsh, is_Zero, Jump, memRead, memToReg, memWrite,
       not_1_out, or_2_out, RegDst, RegWrite;
  wire [1:0] pcdecoder_1_physical;
  wire [2:0] aluFunc, aluOp;
  wire [4:0] multiplexer_4_out;
  wire [5:0] Func, Opcode;
  wire [7:0] pcdecoder_1_physical_2;
  wire [10:0] A;
  wire [27:8] shift_Jump;
  wire [31:0] add_1_s, Data_Mem_d, High_q, highOpc, Low_q, lowOpc, multiplexer_1_out, multiplexer_2_out,
       multiplexer_3_out, multiplexer_5_out, multiplexer_6_out, Pc_plus_4, PC_q, Reg_File_da, Reg_File_db,
       res;
  wire [31:2] shift2;
  wire [31:30] bitextender_1_out;

  Multiplexer #(.Bits(32)) multiplexer_1 (.sel(bsh), .in_0(Pc_plus_4), .in_1(add_1_s), .out(multiplexer_1_out));
  Add #(.Bits(32)) add_1 (.a(Pc_plus_4), .b({shift2, 2'b00}), .c_i(1'b0), .s(add_1_s));  // open: c_o
  Multiplexer #(.Bits(32)) multiplexer_2 (
    .sel(Jump), .in_0(multiplexer_1_out), .in_1({Pc_plus_4[31:28], shift_Jump, Func, 2'b00}),
    .out(multiplexer_2_out));
  Multiplexer #(.Bits(32)) multiplexer_3 (
    .sel(rst), .in_0(multiplexer_2_out), .in_1(32'h400000), .out(multiplexer_3_out));
  not not_1 (not_1_out, is_Zero);
  Register #(.Bits(32)) PC (.D(multiplexer_3_out), .C(clk), .en(1'b1), .Q(PC_q));
  and and_1 (and_1_out, Branch_Out, is_Zero);
  and and_2 (and_2_out, Bne, not_1_out);
  Add #(.Bits(32)) add_2 (.a(PC_q), .b(32'h4), .c_i(1'b0), .s(Pc_plus_4));  // open: c_o
  pcdecoder pcdecoder_1 (.Pc(PC_q), .Physical({pcdecoder_1_physical_2, pcdecoder_1_physical}), .Invalid_pc(invalid_pc));
  or or_1 (bsh, and_1_out, and_2_out);
  ROM #(.AddrBits(8), .Bits(32)) InstMem (.A(pcdecoder_1_physical_2), .sel(1'b1), .D({Opcode, shift_Jump, Func}));
  ControlUnit controlunit_1 (
    .Opcode(Opcode), .Reset(rst), .aluSrc(aluSrc), .RegDst(RegDst), .aluOp(aluOp), .memToReg(memToReg),
    .memRead(memRead), .memWrite(memWrite), .RegWrite(RegWrite), .branchNotEqual(Branch_Out),
    .branchEqual(Jump), .Jump(Bne));
  or or_2 (or_2_out, memWrite, memRead);
  // memdecoder memdecoder_1: pin names not known; wires that end beside it: or_2_out, res, A, invalid_addr
  Multiplexer #(.Bits(5)) multiplexer_4 (
    .sel(RegDst), .in_0(shift_Jump[22:18]), .in_1(shift_Jump[17:13]), .out(multiplexer_4_out));
  ALUControl alucontrol_1 (.aluOp(aluOp), .Func(Func), .aluFunc(aluFunc));
  BitExtender #(.inputBits(16), .outputBits(32)) bitextender_1 (
    .in({shift_Jump[17:8], Func}), .out({bitextender_1_out, shift2}));
  RegisterFile #(.AddrBits(5), .Bits(32)) Reg_File (
    .Din(multiplexer_6_out), .we(RegWrite), .Rw(multiplexer_4_out), .C(clk), .Ra(shift_Jump[27:23]),
    .Rb(shift_Jump[22:18]), .Da(Reg_File_da), .Db(Reg_File_db));
  Multiplexer #(.Bits(32)) multiplexer_5 (
    .sel(aluSrc), .in_0(Reg_File_db), .in_1({bitextender_1_out, shift2}), .out(multiplexer_5_out));
  ALU alu_1 (
    .a(Reg_File_da), .b(multiplexer_5_out), .op(aluFunc), .res(res), .isZero(is_Zero), .lower(lowOpc),
    .higher(highOpc));
  RAMDualPort #(.AddrBits(11), .Bits(32)) Data_Mem (
    .A({2'b00, A[10:2]}), .Din(Reg_File_db), .str(memWrite), .C(clk), .ld(memRead), .D(Data_Mem_d));
  Multiplexer #(.Bits(32)) multiplexer_6 (.sel(memToReg), .in_0(res), .in_1(Data_Mem_d), .out(multiplexer_6_out));
  Register #(.Bits(32)) Low (.D(lowOpc), .C(clk), .en(1'b0), .Q(Low_q));
  Register #(.Bits(32)) High (.D(highOpc), .C(clk), .en(1'b0), .Q(High_q));

  assign invalid_opcode = 1'b0;

  // Other names for the same wires on the sheet: shift_Jump (some bits) = {Pc_plus_4[31:28], Func}

  // Notes on the sheet:
  //   contents of InstMem (hex, n*v repeats v):
  //   8c080000,8c090004,ac080008
endmodule
