// Digital circuit decorder.dig as structural Verilog
module decorder (
  input  PC,
  output Invalid,
  output Physical
);

  wire mayor, menor;
  wire [9:0] undriven;

  Comparator comparator_1 (.a(PC), .b(1'b0), .lt(menor));  // open: gt, eq
  Comparator comparator_2 (.a(PC), .b(1'b1), .gt(mayor));  // open: eq, lt
  or or_1 (Invalid, mayor, menor);
  Multiplexer multiplexer_1 (.sel(Invalid), .in_0(undriven[0]), .in_1(1'b0), .out(Physical));
  // Pins of 1 and 10 bits meet at undriven

  // Other names for the same wires on the sheet: res = Invalid
endmodule
