// Digital circuit pcdecoder.dig as structural Verilog
module pcdecoder (
  input  [31:0] Pc,
  output [9:0] Physical,
  output Invalid_pc
);

  wire is_greater, is_less;

  or or_1 (Invalid_pc, is_greater, is_less);
  Comparator #(.Bits(32)) comparator_1 (.a(Pc), .b(32'h400000), .lt(is_less));  // open: gt, eq
  Comparator #(.Bits(32)) comparator_2 (.a(Pc), .b(32'h4003ff), .gt(is_greater));  // open: eq, lt
  Multiplexer #(.Bits(10)) multiplexer_1 (.sel(Invalid_pc), .in_0(Pc[9:0]), .in_1({10{1'b0}}), .out(Physical));

  // Other names for the same wires on the sheet: res = Invalid_pc
endmodule
